# Fritzing sketch RAM-16 (saved by Fritzing 0.9.6b)
breadboards: 4

parts:
  U3 = 74HC245 [package="DIP (Dual Inline) [THT]"]
  U4 = 74HC245 [package="DIP (Dual Inline) [THT]"]
  U7 = 74HC20 [package="DIP (Dual Inline) [THT]"]
  U8 = 74HC00 [package="DIP (Dual Inline) [THT]"]
  U9 = 74HC08 [package="DIP (Dual Inline) [THT]"]
  U10 = 74HC139 [package="DIP (Dual Inline) [THT]"]
  U11 = AS6C6264 [package="DIP (Dual Inline) [THT]"]
  U12 = AS6C6264 [package="DIP (Dual Inline) [THT]"]
  U13 = AS6C6264 [package="DIP (Dual Inline) [THT]"]
  U14 = AS6C6264 [package="DIP (Dual Inline) [THT]"]
  U17 = 74HC245 [package="DIP (Dual Inline) [THT]"]
  U18 = 74HC157 [package="DIP (Dual Inline) [THT]"]
  U19 = 74HC32 [package="DIP (Dual Inline) [THT]"]

nets:
  N1: U3.DIR, U4.DIR, U10.1Y3#, U11./OE, U12./OE, U13./OE, U14./OE, U17.DIR
  N2: U3.A1, U3.A8
  GND: U3.GND, U4.GND, U13.A0, U13.Vss, U14.A0, U17.GND
  N3: U3.B8, U3.B1
  N4: U3./DIR, U17./DIR, U19.3Y
  VCC: U3.Vcc, U4.Vcc, U17.Vcc
  N5: U4.A1, U4.A8
  N6: U4.B8, U4.B1
  N7: U4./DIR, U19.4Y
  N8: U7.1A, U7.1D
  N9: U7.1Y, U8.1B, U8.2B, U11.CE2, U12.CE2, U13.CE2, U14.CE2
  N10: U7.2A, U7.2D
  N11: U8.1Y, U19.4B
  N12: U8.2A, U8.3Y, U9.3Y
  N13: U8.2Y, U19.3B
  GND_2: U8.GND, U9.1A, U9.1B, U9.2A, U9.2B, U9.GND, U10.GND, U18.GND
  VCC_2: U8.3A, U8.Vcc, U9.3B, U9.Vcc, U10.VCC, U11.Vcc, U12.Vcc, U18.VCC
  N14: U8.3B, U9.3A, U10.2A0
  N15: U8.4Y, U18.3in0, U18.4in0
  N16: U8.4A, U8.4B, U10.2A1, U10.2E#, U18.1in0, U18.2in0
  N17: U9.4A, U9.4B, U18.E#, U19.1A, U19.1B, U19.GND
  N18: U10.1E#, U10.1Y1#
  N19: U10.1Y2#, U19.2A
  N20: U10.2Y3#, U18.4in1
  N21: U10.2Y2#, U18.3in1
  N22: U10.2Y1#, U18.2in1
  N23: U10.2Y0#, U18.1in1
  N24: U11.A12, U11.A1
  N25: U11.A0, U12.A0
  N26: U11.DQ0, U11.A8
  VSS: U11.Vss, U12.Vss
  N27: U11./CE, U18.4Y#
  N28: U11./WE, U12./WE, U13./WE, U14./WE, U19.2Y
  N29: U12.A12, U12.A1
  N30: U12.DQ0, U12.A8
  N31: U12./CE, U18.3Y#
  N32: U13.A12, U13.A1
  N33: U13.DQ0, U13.A8
  N34: U13./CE, U18.1Y#
  VCC_3: U13.Vcc, U14.Vcc
  N35: U14.A12, U14.A1
  N36: U14.DQ0, U14.A8
  N37: U14./CE, U18.2Y#
  N38: U17.A1, U17.A8
  N39: U17.B8, U17.B1
  N40: U18.S, U19.Vcc
  N41: U19.2B, U19.3A, U19.4A

notes:
  Mem High
  Sys High
  Mem High
  Sys Low
  Mem Low
  Sys Low

custom parts:
  74HC245: 8-bit bidrectional transceiver with straight-across pinout
  74HC20: Dual 4-input NAND gate
  74HC00: Quad NAND. The original 74xx part.
  74HC08: Quad positive AND gate
  74HC139: Dual 2-to-4 decoders with active low enable
  AS6C6264: 8k x 8 bit CMOS static RAM
  74HC157: Quad 2:1 mux
  74HC32: Quad 2-input OR gate
